# Fritzing sketch Tåg (saved by Fritzing 0.9.1b)
breadboards: 1

parts:
  Part1 = Arduino Uno (Rev3)
  M1 = DC Motor
  M2 = DC Motor
  M3 = DC Motor
  R1 = Resistor [tolerance=±5% resistance=470 package=THT]
  S1 = Pushbutton [package=THT]
  S2 = Pushbutton [package=THT]
  S3 = Pushbutton [package=THT]
  S4 = Pushbutton [package=THT]
  S5 = Pushbutton [package=THT]
  S6 = Pushbutton [package=THT]
  S7 = Pushbutton [package=THT]
  S8 = Pushbutton [package=THT]
  S9 = Pushbutton [package=THT]

nets:
  N1: Part1.D8, S1.leg0, S2.leg0, S3.leg0
  N2: Part1.D9_PWM, S4.leg0, S5.leg0, S6.leg0
  N3: Part1.D10_PWM/SS, S7.leg0, S8.leg0, S9.leg0
  N4: Part1.GND, M1.pin_2, M2.pin_2, M3.pin_2
  N5: Part1.D2, M2.pin_1
  N6: Part1.D3_PWM, M3.pin_1
  N7: Part1.D4, M1.pin_1
  N8: Part1.5V, R1.Pin_0
  N9: R1.Pin_1, S1.leg1, S2.leg1, S3.leg1, S4.leg1, S6.leg1, S7.leg1, S8.leg1, S9.leg1

// code stored in the sketch: Tσg.ino
//Variables
const int fIn = 8;
const int sIn = 9;
const int tIn = 10;

const int fMotor = 2;
const int sMotor = 3;
const int tMotor = 4;

void setup() {

}
